# Fritzing sketch Titan Layout (saved by Fritzing 0.9.2b)

parts:
  BAT1 = Battery Holders [package=lipo-1100mAh]
  J1 = Piezo Speaker
  U2 = Naze 32 Rev 5 [package=dip]
  U1 = MinimOSD [package=dip]
  U3 = ESC [package=dip]  # not connected
  U4 = ESC [package=dip]  # not connected
  U5 = ESC [package=dip]  # not connected
  U6 = ESC [package=dip]  # not connected
  U7 = BEC [package=dip]  # not connected
  U8 = BEC [package=dip]  # not connected
  U9 = FrSky D4R-II [package=dip]  # not connected

nets:
  N1: BAT1.+, U2.BAT+
  N2: BAT1.-, U1.GND#1
  N3: J1.pin1, U2.BUZZ-
  N4: J1.pin2, U2.BUZZ+
  N5: U2.TX, U1.TX
  N6: U2.RX, U1.RX

custom parts:
  Naze 32 Rev 5: Naze 32 Revision 5 (10DoF)
  MinimOSD: Minim OSD Micro/Mini
  ESC: Electronic Speed Control for Brushless Motor. Without built in BEC
  BEC: Battery Elimination Circuit Has an adjustable voltage output depending on trimmer pot.
  FrSky D4R-II: FrSky 4 channel (cPPM 8 channel) receiver
